# Fritzing sketch electric Fence (saved by Fritzing 0.9.3b)

parts:
  Part1 = Arduino Mega 2560 (Rev3)
  ESP32_-_Back1 = ESP32 - CAM
  GY1 = MPU-6050 Board GY-521 [form="♀ (female)" package=THT]
  GY2 = MPU-6050 Board GY-521 [form="♀ (female)" package=THT]
  GY3 = MPU-6050 Board GY-521 [form="♀ (female)" package=THT]
  GY4 = MPU-6050 Board GY-521 [form="♀ (female)" package=THT]
  PIR1 = PIR sensor
  PIR2 = PIR sensor
  PIR3 = PIR sensor
  PIR4 = PIR sensor
  M1 = NEO-M8N GPS Module [part_number=GY-GPSV3-NEO]
  R1 = Photocell (LDR) [package=THT]
  LED1 = LEDs [package=led10mm]
  Mod1 = KY-019 5V Relay Module [package="Breakout board"]

nets:
  N1: Part1.A0, R1.pin_0
  N2: Part1.D21/SCL, GY1.pin3, GY2.pin3, GY3.pin3, GY4.pin3
  N3: Part1.D20/SDA, GY1.pin4, GY2.pin4, GY3.pin4, GY4.pin4
  GND: Part1.GND, Part1.RESET, ESP32_-_Back1.GND#16, GY1.pin2, GY2.pin2, GY3.pin2, GY4.pin2, PIR1.GND, PIR2.GND, PIR3.GND, PIR4.GND, M1.GND, R1.pin_1, LED1.C, Mod1.-
  N4: Part1.D9_PWM, M1.Tx
  N5: Part1.D8_PWM, M1.Rx
  3V3: Part1.3V3, M1.Vcc
  VDD: Part1.5V, ESP32_-_Back1.3.3V_/_5V_/_P_OUT, GY1.pin1, GY2.pin1, GY3.pin1, GY4.pin1, PIR1.VDD, PIR2.VDD, PIR3.VDD, PIR4.VDD, Mod1.+
  N6: Part1.D0_RX0, ESP32_-_Back1.GPIO1_/_TX
  N7: Part1.D1_TX0, ESP32_-_Back1.GPIO3_/_RX
  N8: Part1.D2_PWM, PIR1.SIG
  N9: Part1.D3_PWM, PIR2.SIG
  N10: Part1.D4_PWM, PIR3.SIG
  N11: Part1.D5_PWM, PIR4.SIG
  N12: Part1.D6_PWM, LED1.A
  N13: Part1.D7_PWM, Mod1.S
  N14: ESP32_-_Back1.GPIO0, ESP32_-_Back1.GND#12

custom parts:
  ESP32 - CAM: The ESP32-CAM has a very competitive small-size camera module that can operate independently as a minimum system with a footprint of only 27*40.5*4.5mm and a deep sleep current of up to 6mA.
  MPU-6050 Board GY-521: Acelerometro y Giroscopio MPU-6050 Board GY-521
  NEO-M8N GPS Module: GY-GPSV3-NEO NEO-M8N GPS Module Module based on U-blox NEO-M8N GPS engine, incorporating regulator for 3.3-5V DC input, MS621FE-compatible rechargeable battery for backup and EEPROM for storing configuration settings. Links: NEO-M8 series Product Summary NEO-M8 Datasheet
  KY-019 5V Relay Module: KY-019 5V Relay module, used to control AC circuits. (Special thanks to vanepp for fixing the PCB holes and other errors)
